// Logisim project LogisimSimulation.circ as structural Verilog: 3 circuits, main circuit main
module main (
  input  [5:0] in_1,
  input  [4:0] in_2,
  input  [4:0] in_3,
  input  [2:0] in_4,
  input  [2:0] in_5,
  input  [5:0] in_6,
  input  [4:0] in_7,
  input  [4:0] in_8,
  input  [5:0] in_9,
  input  [4:0] in_10,
  input  [4:0] in_11,
  input  [5:0] in_12,
  input  [4:0] in_13,
  input  [4:0] in_14,
  input  [5:0] in_15,
  input  [4:0] in_16,
  input  [4:0] in_17,
  input  [2:0] in_18,
  input  [2:0] in_19,
  input  [5:0] in_20,
  input  [4:0] in_21,
  input  [2:0] in_22,
  input  [2:0] in_23,
  output [15:0] out_24,
  output out_25
);

  wire adder_1_cout, adder_2_cout, adder_3_cout;
  wire [2:0] adder_1_out, adder_2_out, multiplier_1_cout, multiplier_1_out, multiplier_2_cout,
       multiplier_2_out;
  wire [4:0] bit_extender_1_out, bit_extender_2_out;
  wire [6:0] adder_3_out, adder_4_out, bit_extender_3_out, bit_extender_4_out, bit_extender_5_out,
       shifter_1_out, shifter_2_out;
  wire [15:0] A_out_6, and_2_out, and_4_out, and_5_out, limitchecker_1_out_7, limitchecker_2_out_7,
       limitchecker_3_out_7, limitchecker_4_out_7, limitchecker_5_out_7, subscriptionweight_1_out_6,
       subscriptionweight_2_out_6, subscriptionweight_3_out_6, subscriptionweight_4_out_6;

  assign bit_extender_1_out = {{2{1'b0}}, in_22};  // Bit_Extender bit_extender_1
  assign bit_extender_2_out = {{2{1'b0}}, in_23};  // Bit_Extender bit_extender_2
  SubscriptionWeight A (
    .in_1(in_2), .in_2(bit_extender_1_out), .in_3(in_3), .in_4(bit_extender_2_out), .in_5(in_1),
    .out_6(A_out_6));
  SubscriptionWeight subscriptionweight_1 (
    .in_1(in_7), .in_2(bit_extender_1_out), .in_3(in_8), .in_4(bit_extender_2_out), .in_5(in_6),
    .out_6(subscriptionweight_1_out_6));
  Multiplier #(.width(3)) multiplier_1 (
    .a(in_4), .b(in_5), .out(multiplier_1_out), .cin(3'b000), .cout(multiplier_1_cout));
  Multiplier #(.width(3)) multiplier_2 (
    .a(in_18), .b(in_19), .out(multiplier_2_out), .cin(3'b000), .cout(multiplier_2_cout));
  Adder #(.width(3)) adder_1 (
    .a(multiplier_1_out), .b(multiplier_2_out), .out(adder_1_out), .cin(1'b0), .cout(adder_1_cout));
  assign bit_extender_3_out = {{4{1'b0}}, adder_1_out};  // Bit_Extender bit_extender_3
  Adder #(.width(3)) adder_2 (
    .a(multiplier_1_cout), .b(multiplier_2_cout), .out(adder_2_out), .cin(adder_1_cout), .cout(adder_2_cout));
  assign bit_extender_4_out = {{4{1'b0}}, adder_2_out};  // Bit_Extender bit_extender_4
  assign bit_extender_5_out = {{6{1'b0}}, adder_2_cout};  // Bit_Extender bit_extender_5
  SubscriptionWeight subscriptionweight_2 (
    .in_1(in_10), .in_2(bit_extender_1_out), .in_3(in_11), .in_4(bit_extender_2_out), .in_5(in_9),
    .out_6(subscriptionweight_2_out_6));
  Adder #(.width(7)) adder_3 (
    .a(bit_extender_3_out), .b(shifter_1_out), .out(adder_3_out), .cin(1'b0), .cout(adder_3_cout));
  Shifter #(.width(7)) shifter_1 (.in(bit_extender_4_out), .\dist (3'b011), .out(shifter_1_out));
  Shifter #(.width(7)) shifter_2 (.in(bit_extender_5_out), .\dist (3'b110), .out(shifter_2_out));
  SubscriptionWeight subscriptionweight_3 (
    .in_1(in_13), .in_2(bit_extender_1_out), .in_3(in_14), .in_4(bit_extender_2_out), .in_5(in_12),
    .out_6(subscriptionweight_3_out_6));
  Adder #(.width(7)) adder_4 (.a(adder_3_out), .b(shifter_2_out), .out(adder_4_out), .cin(adder_3_cout));  // open: cout
  SubscriptionWeight subscriptionweight_4 (
    .in_1(in_16), .in_2(bit_extender_1_out), .in_3(in_17), .in_4(bit_extender_2_out), .in_5(in_15),
    .out_6(subscriptionweight_4_out_6));
  Limitchecker limitchecker_1 (
    .in_1(in_2), .in_2(adder_4_out), .in_3(in_3), .in_4(in_21), .in_5(in_1), .in_6(in_20),
    .out_7(limitchecker_1_out_7));
  Limitchecker limitchecker_2 (
    .in_1(in_7), .in_2(adder_4_out), .in_3(in_8), .in_4(in_21), .in_5(in_6), .in_6(in_20),
    .out_7(limitchecker_2_out_7));
  Limitchecker limitchecker_3 (
    .in_1(in_10), .in_2(adder_4_out), .in_3(in_11), .in_4(in_21), .in_5(in_9), .in_6(in_20),
    .out_7(limitchecker_3_out_7));
  Limitchecker limitchecker_4 (
    .in_1(in_13), .in_2(adder_4_out), .in_3(in_14), .in_4(in_21), .in_5(in_12), .in_6(in_20),
    .out_7(limitchecker_4_out_7));
  Limitchecker limitchecker_5 (
    .in_1(in_16), .in_2(adder_4_out), .in_3(in_17), .in_4(in_21), .in_5(in_15), .in_6(in_20),
    .out_7(limitchecker_5_out_7));
  assign out_24 = limitchecker_1_out_7 & A_out_6;  // AND_Gate and_1, 16 bits wide
  assign and_2_out = limitchecker_2_out_7 & subscriptionweight_1_out_6;  // AND_Gate and_2, 16 bits wide
  // AND_Gate and_3 has open pins: in0=limitchecker_3_out_7, in1=subscriptionweight_2_out_6, out=open
  assign and_4_out = limitchecker_4_out_7 & subscriptionweight_3_out_6;  // AND_Gate and_4, 16 bits wide
  assign and_5_out = limitchecker_5_out_7 & subscriptionweight_4_out_6;  // AND_Gate and_5, 16 bits wide
  Comparator #(.width(16)) comparator_1 (.a(out_24), .b(and_2_out), .eq(out_25));  // open: gt, lt
  Comparator #(.width(16)) comparator_2 (.a(and_4_out), .b(and_5_out));  // open: gt, eq, lt
endmodule

module SubscriptionWeight (
  input  [4:0] in_1,
  input  [4:0] in_2,
  input  [4:0] in_3,
  input  [4:0] in_4,
  input  [5:0] in_5,
  output [15:0] out_6
);

  wire [4:0] multiplier_1_cout, multiplier_1_out, multiplier_2_cout, multiplier_2_out;
  wire [9:0] adder_1_out, adder_2_out, adder_3_out, bit_extender_1_out, bit_extender_2_out,
       bit_extender_3_out, bit_extender_4_out, shifter_1_out, shifter_2_out;
  wire [15:0] bit_extender_5_out, bit_extender_6_out, shifter_3_out;

  Multiplier #(.width(5)) multiplier_1 (
    .a(in_1), .b(in_2), .out(multiplier_1_out), .cin({5{1'b0}}), .cout(multiplier_1_cout));
  Multiplier #(.width(5)) multiplier_2 (
    .a(in_3), .b(in_4), .out(multiplier_2_out), .cin({5{1'b0}}), .cout(multiplier_2_cout));
  assign bit_extender_1_out = {{5{1'b0}}, multiplier_1_out};  // Bit_Extender bit_extender_1
  assign bit_extender_2_out = {{5{1'b0}}, multiplier_1_cout};  // Bit_Extender bit_extender_2
  assign bit_extender_3_out = {{5{1'b0}}, multiplier_2_out};  // Bit_Extender bit_extender_3
  assign bit_extender_4_out = {{5{1'b0}}, multiplier_2_cout};  // Bit_Extender bit_extender_4
  assign bit_extender_5_out = {{10{1'b0}}, in_5};  // Bit_Extender bit_extender_5
  Shifter #(.width(10)) shifter_1 (.in(bit_extender_2_out), .\dist (4'b0101), .out(shifter_1_out));
  Shifter #(.width(10)) shifter_2 (.in(bit_extender_4_out), .\dist (4'b0101), .out(shifter_2_out));
  Adder #(.width(10)) adder_1 (.a(bit_extender_1_out), .b(shifter_1_out), .out(adder_1_out), .cin(1'b0));  // open: cout
  Adder #(.width(10)) adder_2 (.a(bit_extender_3_out), .b(shifter_2_out), .out(adder_2_out), .cin(1'b0));  // open: cout
  Adder #(.width(10)) adder_3 (.a(adder_1_out), .b(adder_2_out), .out(adder_3_out), .cin(1'b0));  // open: cout
  assign bit_extender_6_out = {{6{1'b0}}, adder_3_out};  // Bit_Extender bit_extender_6
  Shifter #(.width(16)) shifter_3 (.in(bit_extender_6_out), .\dist (4'b0110), .out(shifter_3_out));
  Divider #(.width(16)) divider_1 (
    .a({16{1'b0}}), .b(bit_extender_5_out), .out(out_6), .upper(shifter_3_out));  // open: rem
endmodule

module Limitchecker (
  input  [4:0] in_1,
  input  [6:0] in_2,
  input  [4:0] in_3,
  input  [4:0] in_4,
  input  [5:0] in_5,
  input  [5:0] in_6,
  output [15:0] out_7
);

  wire and_1_out, comparator_1_lt, comparator_2_gt, comparator_3_lt, not_1_out, not_2_out, not_3_out;
  wire [6:0] bit_extender_1_out;

  assign bit_extender_1_out = {{2{1'b0}}, in_1};  // Bit_Extender bit_extender_1
  Comparator #(.width(5)) comparator_1 (.a(in_3), .b(in_4), .lt(comparator_1_lt));  // open: gt, eq
  Comparator #(.width(6)) comparator_2 (.a(in_5), .b(in_6), .gt(comparator_2_gt));  // open: eq, lt
  Comparator #(.width(7)) comparator_3 (.a(bit_extender_1_out), .b(in_2), .lt(comparator_3_lt));  // open: gt, eq
  not not_1 (not_1_out, comparator_3_lt);
  not not_2 (not_2_out, comparator_1_lt);
  not not_3 (not_3_out, comparator_2_gt);
  and and_1 (and_1_out, not_1_out, not_2_out, not_3_out);
  assign out_7 = {{15{and_1_out}}, and_1_out};  // Bit_Extender bit_extender_2
endmodule
